// Logisim project Banc_de_registre.circ as structural Verilog: 4 circuits, main circuit main
module main (
  input  [3:0] rd,
  input  [3:0] rt,
  input  [3:0] rs,
  input  [7:0] ValIn,
  input  Reset,
  input  regWrite,
  input  Horloge,
  output [7:0] R___rt,
  output [7:0] R___rs
);

  wire decoder_1_out0, decoder_1_out1, decoder_1_out2, decoder_1_out3, decoder_1_out4, decoder_1_out5,
       decoder_1_out6, decoder_1_out7, decoder_1_out8, decoder_1_out9, decoder_1_out10, decoder_1_out11,
       decoder_1_out12, decoder_1_out13, decoder_1_out14, decoder_1_out15, not_1_out;
  wire [7:0] register_1_q, register_2_q, register_3_q, register_4_q, register_5_q, register_6_q,
       register_7_q, register_8_q, register_9_q, register_10_q, register_11_q, register_12_q, register_13_q,
       register_14_q, register_15_q, register_16_q;

  Decoder #(.select(4), .disabled(0)) decoder_1 (
    .out0(decoder_1_out0), .out1(decoder_1_out1), .out2(decoder_1_out2), .out3(decoder_1_out3),
    .out4(decoder_1_out4), .out5(decoder_1_out5), .out6(decoder_1_out6), .out7(decoder_1_out7),
    .out8(decoder_1_out8), .out9(decoder_1_out9), .out10(decoder_1_out10), .out11(decoder_1_out11),
    .out12(decoder_1_out12), .out13(decoder_1_out13), .out14(decoder_1_out14), .out15(decoder_1_out15),
    .sel(rd), .en(regWrite));
  not not_1 (not_1_out, Horloge);
  Register register_1 (.D(ValIn), .en(decoder_1_out0), .Q(register_1_q), .clk(not_1_out), .clr(Reset));
  Register register_2 (.D(ValIn), .en(decoder_1_out1), .Q(register_2_q), .clk(not_1_out), .clr(Reset));
  Register register_3 (.D(ValIn), .en(decoder_1_out2), .Q(register_3_q), .clk(not_1_out), .clr(Reset));
  Register register_4 (.D(ValIn), .en(decoder_1_out3), .Q(register_4_q), .clk(not_1_out), .clr(Reset));
  Register register_5 (.D(ValIn), .en(decoder_1_out4), .Q(register_5_q), .clk(not_1_out), .clr(Reset));
  Register register_6 (.D(ValIn), .en(decoder_1_out5), .Q(register_6_q), .clk(not_1_out), .clr(Reset));
  Register register_7 (.D(ValIn), .en(decoder_1_out6), .Q(register_7_q), .clk(not_1_out), .clr(Reset));
  Register register_8 (.D(ValIn), .en(decoder_1_out7), .Q(register_8_q), .clk(not_1_out), .clr(Reset));
  Register register_9 (.D(ValIn), .en(decoder_1_out8), .Q(register_9_q), .clk(not_1_out), .clr(Reset));
  Register register_10 (.D(ValIn), .en(decoder_1_out9), .Q(register_10_q), .clk(not_1_out), .clr(Reset));
  Register register_11 (.D(ValIn), .en(decoder_1_out10), .Q(register_11_q), .clk(not_1_out), .clr(Reset));
  Register register_12 (.D(ValIn), .en(decoder_1_out11), .Q(register_12_q), .clk(not_1_out), .clr(Reset));
  Register register_13 (.D(ValIn), .en(decoder_1_out12), .Q(register_13_q), .clk(not_1_out), .clr(Reset));
  Register register_14 (.D(ValIn), .en(decoder_1_out13), .Q(register_14_q), .clk(not_1_out), .clr(Reset));
  Register register_15 (.D(ValIn), .en(decoder_1_out14), .Q(register_15_q), .clk(not_1_out), .clr(Reset));
  Register register_16 (.D(ValIn), .en(decoder_1_out15), .Q(register_16_q), .clk(not_1_out), .clr(Reset));
  Multiplexer #(.select(4), .width(8), .enable("false")) multiplexer_1 (
    .in0(register_1_q), .in1(register_2_q), .in2(register_3_q), .in3(register_4_q), .in4(register_5_q),
    .in5(register_6_q), .in6(register_7_q), .in7(register_8_q), .in8(register_9_q), .in9(register_10_q),
    .in10(register_11_q), .in11(register_12_q), .in12(register_13_q), .in13(register_14_q),
    .in14(register_15_q), .in15(register_16_q), .out(R___rt), .sel(rt));
  Multiplexer #(.select(4), .width(8), .enable("false")) multiplexer_2 (
    .in0(register_1_q), .in1(register_2_q), .in2(register_3_q), .in3(register_4_q), .in4(register_5_q),
    .in5(register_6_q), .in6(register_7_q), .in7(register_8_q), .in8(register_9_q), .in9(register_10_q),
    .in10(register_11_q), .in11(register_12_q), .in12(register_13_q), .in13(register_14_q),
    .in14(register_15_q), .in15(register_16_q), .out(R___rs), .sel(rs));
endmodule

module Registre_8bits (
  input  [7:0] A,
  output [7:0] A_2
);

  wire clock_1_out;

  Clock clock_1 (.out(clock_1_out));
  BasculeD basculed_1 (.H(A[0]), .D(clock_1_out), .out_3(A_2[0]));
  BasculeD basculed_2 (.H(A[1]), .D(clock_1_out), .out_3(A_2[1]));
  BasculeD basculed_3 (.H(A[2]), .D(clock_1_out), .out_3(A_2[2]));
  BasculeD basculed_4 (.H(A[3]), .D(clock_1_out), .out_3(A_2[3]));
  BasculeD basculed_5 (.H(A[4]), .D(clock_1_out), .out_3(A_2[4]));
  BasculeD basculed_6 (.H(A[5]), .D(clock_1_out), .out_3(A_2[5]));
  BasculeD basculed_7 (.H(A[6]), .D(clock_1_out), .out_3(A_2[6]));
  BasculeD basculed_8 (.H(A[7]), .D(clock_1_out), .out_3(A_2[7]));
endmodule

module BasculeD (
  input  H,
  input  D,
  output out_3
);

  wire not_1_out;

  not not_1 (not_1_out, D);
  S_R_Flip_Flop s_r_ff_1 (.S(D), .clk(H), .R(not_1_out), .Q(out_3));  // open: Qn, preset, reset, en

  // Notes on the sheet:
  //   Bascule D pour l'utilisation du registre 8 bits.
endmodule

module register2 (
  input  [3:0] rd,
  input  [3:0] rt,
  input  [3:0] rs,
  input  [7:0] ValIn,
  input  regWrite,
  output [7:0] R___rs,
  output [7:0] R___rt
);

  wire and_1_out, and_2_out, and_3_out, and_4_out, and_5_out, and_6_out, and_7_out, and_8_out, and_9_out,
       and_10_out, and_11_out, and_12_out, and_13_out, and_14_out, and_15_out, and_16_out, and_17_out,
       decoder_1_out0, decoder_1_out1, decoder_1_out2, decoder_1_out3, decoder_1_out4, decoder_1_out5,
       decoder_1_out6, decoder_1_out7, decoder_1_out8, decoder_1_out9, decoder_1_out10, decoder_1_out11,
       decoder_1_out12, decoder_1_out13, decoder_1_out14, decoder_1_out15, Horloge_out;
  wire [7:0] register_1_q, register_2_q, register_3_q, register_4_q, register_5_q, register_6_q,
       register_7_q, register_8_q, register_9_q, register_10_q, register_11_q, register_12_q, register_13_q,
       register_14_q, register_15_q, register_16_q;

  Decoder #(.select(4), .enable("false")) decoder_1 (
    .out0(decoder_1_out0), .out1(decoder_1_out1), .out2(decoder_1_out2), .out3(decoder_1_out3),
    .out4(decoder_1_out4), .out5(decoder_1_out5), .out6(decoder_1_out6), .out7(decoder_1_out7),
    .out8(decoder_1_out8), .out9(decoder_1_out9), .out10(decoder_1_out10), .out11(decoder_1_out11),
    .out12(decoder_1_out12), .out13(decoder_1_out13), .out14(decoder_1_out14), .out15(decoder_1_out15),
    .sel(rd));
  Clock Horloge (.out(Horloge_out));
  and and_1 (and_1_out, Horloge_out, regWrite);
  and and_2 (and_2_out, and_1_out, decoder_1_out0);
  and and_3 (and_3_out, and_1_out, decoder_1_out1);
  and and_4 (and_4_out, and_1_out, decoder_1_out2);
  and and_5 (and_5_out, and_1_out, decoder_1_out3);
  and and_6 (and_6_out, and_1_out, decoder_1_out4);
  and and_7 (and_7_out, and_1_out, decoder_1_out5);
  and and_8 (and_8_out, and_1_out, decoder_1_out6);
  and and_9 (and_9_out, and_1_out, decoder_1_out7);
  and and_10 (and_10_out, and_1_out, decoder_1_out8);
  and and_11 (and_11_out, and_1_out, decoder_1_out9);
  and and_12 (and_12_out, and_1_out, decoder_1_out10);
  and and_13 (and_13_out, and_1_out, decoder_1_out11);
  and and_14 (and_14_out, and_1_out, decoder_1_out12);
  and and_15 (and_15_out, and_1_out, decoder_1_out13);
  and and_16 (and_16_out, and_1_out, decoder_1_out14);
  and and_17 (and_17_out, and_1_out, decoder_1_out15);
  Register register_1 (.D(ValIn), .en(and_2_out), .Q(register_1_q));  // open: clk, clr
  Register register_2 (.D(ValIn), .en(and_3_out), .Q(register_2_q));  // open: clk, clr
  Register register_3 (.D(ValIn), .en(and_4_out), .Q(register_3_q));  // open: clk, clr
  Register register_4 (.D(ValIn), .en(and_5_out), .Q(register_4_q));  // open: clk, clr
  Register register_5 (.D(ValIn), .en(and_6_out), .Q(register_5_q));  // open: clk, clr
  Register register_6 (.D(ValIn), .en(and_7_out), .Q(register_6_q));  // open: clk, clr
  Register register_7 (.D(ValIn), .en(and_8_out), .Q(register_7_q));  // open: clk, clr
  Register register_8 (.D(ValIn), .en(and_9_out), .Q(register_8_q));  // open: clk, clr
  Register register_9 (.D(ValIn), .en(and_10_out), .Q(register_9_q));  // open: clk, clr
  Register register_10 (.D(ValIn), .en(and_11_out), .Q(register_10_q));  // open: clk, clr
  Register register_11 (.D(ValIn), .en(and_12_out), .Q(register_11_q));  // open: clk, clr
  Register register_12 (.D(ValIn), .en(and_13_out), .Q(register_12_q));  // open: clk, clr
  Register register_13 (.D(ValIn), .en(and_14_out), .Q(register_13_q));  // open: clk, clr
  Register register_14 (.D(ValIn), .en(and_15_out), .Q(register_14_q));  // open: clk, clr
  Register register_15 (.en(and_16_out), .Q(register_15_q));  // open: D, clk, clr
  Register register_16 (.D(ValIn), .en(and_17_out), .Q(register_16_q));  // open: clk, clr
  Multiplexer #(.select(4), .width(8), .enable("false")) multiplexer_1 (
    .in0(register_1_q), .in1(register_2_q), .in2(register_3_q), .in3(register_4_q), .in4(register_5_q),
    .in5(register_6_q), .in6(register_7_q), .in7(register_8_q), .in8(register_9_q), .in9(register_10_q),
    .in10(register_11_q), .in11(register_12_q), .in12(register_13_q), .in13(register_14_q),
    .in14(register_15_q), .in15(register_16_q), .out(R___rs), .sel(rt));
  Multiplexer #(.select(4), .width(8), .enable("false")) multiplexer_2 (
    .in0(register_1_q), .in1(register_2_q), .in2(register_3_q), .in3(register_4_q), .in4(register_5_q),
    .in5(register_6_q), .in6(register_7_q), .in7(register_8_q), .in8(register_9_q), .in9(register_10_q),
    .in10(register_11_q), .in11(register_12_q), .in12(register_13_q), .in13(register_14_q),
    .in14(register_15_q), .in15(register_16_q), .out(R___rt), .sel(rs));
endmodule
