// Logisim project Decodeur_d_instruction.circ as structural Verilog: 5 circuits, main circuit main
module main (
  input  [3:0] OPcode,
  output isJMP,
  output regWrite,
  output isLoad,
  output [2:0] ctrUAL
);

  isJMP isjmp_1 (.OPcode(OPcode), .isJMP(isJMP));
  regWrite regwrite_1 (.OPcode(OPcode), .regWrite(regWrite));
  isLoad isload_1 (.OPcode(OPcode), .isLoad(isLoad));
  ctrUAL ctrual_1 (.OPcode(OPcode), .ctrUAL(ctrUAL));

  // Notes on the sheet:
  //   Décodeur d'instruction
endmodule

module isJMP (
  input  [3:0] OPcode,
  output isJMP
);

  wire and_1_out, and_2_out, and_3_out;

  and and_1 (and_1_out, OPcode[3], OPcode[2]);
  and and_2 (and_2_out, OPcode[3], OPcode[0]);
  or or_1 (isJMP, and_1_out, and_2_out, and_3_out);
  and and_3 (and_3_out, OPcode[3], OPcode[1]);

  // Notes on the sheet:
  //   isJMP
  //   Formule logique : db + da + dc
endmodule

module ctrUAL (
  input  [3:0] OPcode,
  output [2:0] ctrUAL
);

  wire and_1_out, and_2_out, and_3_out, and_4_out;

  or or_1 (ctrUAL[0], OPcode[0], OPcode[3]);
  and and_1 (and_1_out, OPcode[1], ~OPcode[2], ~OPcode[3]);  // AND_Gate
  and and_2 (and_2_out, ~OPcode[0], OPcode[1], ~OPcode[3]);  // AND_Gate
  and and_3 (and_3_out, ~OPcode[0], OPcode[2], ~OPcode[3]);  // AND_Gate
  and and_4 (and_4_out, ~OPcode[1], OPcode[2], ~OPcode[3]);  // AND_Gate
  or or_2 (ctrUAL[1], and_1_out, and_2_out);
  or or_3 (ctrUAL[2], and_3_out, and_4_out);

  // Notes on the sheet:
  //   crtUAL
  //   Formule logique = d + a
  //   Formule logique = !d!cb + !db!a 
  //   Formule logique = !dc!b + !dc!a
endmodule

module isLoad (
  input  [3:0] OPcode,
  output isLoad
);

  and and_1 (isLoad, OPcode[0], OPcode[1], OPcode[2], ~OPcode[3]);  // AND_Gate

  // Notes on the sheet:
  //   isLoad
  //   Formule logique : !dcba
endmodule

module regWrite (
  input  [3:0] OPcode,
  output regWrite
);

  not not_1 (regWrite, OPcode[3]);

  // Notes on the sheet:
  //   regWrite
  //   Formule Logique : non d
endmodule
