// Logisim project Jump Controler.circ as structural Verilog: 13 circuits, main circuit main
module main (
  input  [3:0] flags,
  input  [3:0] opcode,
  output [1:0] nextPCselect
);

  wire not_1_out, not_2_out, opcode_selector_1_halt, opcode_selector_1_jump,
       \opcode_selector_1_opération_arithmétique ;
  wire [1:0] bitselector_1_out, bitselector_2_out, bitselector_3_out, halt_1_newtpcselect,
       jump_1_nextpcselect, op_1_nextpcselect;

  Opcode_Selector opcode_selector_1 (
    .opcode(opcode), .\Opération_Arithmétique (\opcode_selector_1_opération_arithmétique ),
    .Halt(opcode_selector_1_halt), .Jump(opcode_selector_1_jump));
  BitSelector #(.width(2), .group(2)) bitselector_1 (.in(op_1_nextpcselect), .out(bitselector_1_out), .sel(not_1_out));
  OP op_1 (.OP(\opcode_selector_1_opération_arithmétique ), .nextPCselect(op_1_nextpcselect));
  not not_1 (not_1_out, \opcode_selector_1_opération_arithmétique );
  BitSelector #(.width(2), .group(2)) bitselector_2 (
    .in(halt_1_newtpcselect), .out(bitselector_2_out), .sel(not_2_out));
  Halt halt_1 (.Halt(opcode_selector_1_halt), .newtPCselect(halt_1_newtpcselect));
  not not_2 (not_2_out, opcode_selector_1_halt);
  BitSelector #(.width(2), .group(2)) bitselector_3 (
    .in(jump_1_nextpcselect), .out(bitselector_3_out), .sel(opcode_selector_1_jump));
  Jump jump_1 (.Flags(flags), .opcode(opcode), .nextPCselect(jump_1_nextpcselect));
  assign nextPCselect = bitselector_1_out | bitselector_2_out | bitselector_3_out;  // OR_Gate or_1, 2 bits wide
endmodule

module Opcode_Selector (
  input  [3:0] opcode,
  output \Opération_Arithmétique ,
  output Halt,
  output Jump
);

  wire and_1_out, and_2_out, and_3_out, and_4_out, and_5_out, and_6_out, and_7_out, and_8_out, and_10_out,
       and_11_out, and_12_out, and_13_out, and_14_out, and_15_out, and_16_out;

  and and_1 (and_1_out, ~opcode[0], ~opcode[1], ~opcode[2], ~opcode[3]);  // AND_Gate
  and and_2 (and_2_out, opcode[0], ~opcode[1], ~opcode[2], ~opcode[3]);  // AND_Gate
  and and_3 (and_3_out, ~opcode[0], opcode[1], ~opcode[2], ~opcode[3]);  // AND_Gate
  and and_4 (and_4_out, opcode[0], opcode[1], ~opcode[2], ~opcode[3]);  // AND_Gate
  and and_5 (and_5_out, ~opcode[0], ~opcode[1], opcode[2], ~opcode[3]);  // AND_Gate
  and and_6 (and_6_out, opcode[0], ~opcode[1], opcode[2], ~opcode[3]);  // AND_Gate
  and and_7 (and_7_out, ~opcode[0], opcode[1], opcode[2], ~opcode[3]);  // AND_Gate
  and and_8 (and_8_out, opcode[0], opcode[1], opcode[2], ~opcode[3]);  // AND_Gate
  and and_9 (Halt, ~opcode[0], ~opcode[1], ~opcode[2], opcode[3]);  // AND_Gate
  and and_10 (and_10_out, opcode[0], ~opcode[1], ~opcode[2], opcode[3]);  // AND_Gate
  and and_11 (and_11_out, ~opcode[0], opcode[1], ~opcode[2], opcode[3]);  // AND_Gate
  and and_12 (and_12_out, opcode[0], opcode[1], ~opcode[2], opcode[3]);  // AND_Gate
  and and_13 (and_13_out, ~opcode[0], ~opcode[1], opcode[2], opcode[3]);  // AND_Gate
  and and_14 (and_14_out, opcode[0], ~opcode[1], opcode[2], opcode[3]);  // AND_Gate
  and and_15 (and_15_out, ~opcode[0], opcode[1], opcode[2], opcode[3]);  // AND_Gate
  and and_16 (and_16_out, opcode[0], opcode[1], opcode[2], opcode[3]);
  or or_1 (\Opération_Arithmétique , and_1_out, and_2_out, and_3_out, and_4_out, and_5_out, and_6_out, and_7_out, and_8_out);
  nor nor_1 (Jump, and_10_out, and_11_out, and_12_out, and_13_out, and_14_out, and_15_out, and_16_out);
endmodule

module OP (
  input  OP,
  output [1:0] nextPCselect
);

  Multiplexer #(.width(2)) multiplexer_1 (.in0(2'b11), .in1(2'b00), .out(nextPCselect), .sel(OP));  // open: en
endmodule

module Halt (
  input  Halt,
  output [1:0] newtPCselect
);

  Multiplexer #(.width(2)) multiplexer_1 (.in0(2'b11), .in1(2'b01), .out(newtPCselect), .sel(Halt));  // open: en
endmodule

module Jump (
  input  [3:0] Flags,
  input  [3:0] opcode,
  output [1:0] nextPCselect
);

  wire jump_opcode_selector_1_b, jump_opcode_selector_1_beq, jump_opcode_selector_1_bge,
       jump_opcode_selector_1_bgt, jump_opcode_selector_1_ble, jump_opcode_selector_1_blt,
       jump_opcode_selector_1_bne;
  wire [1:0] b_1_s, beq_1_s, bge_1_s, bgt_1_s, ble_1_s, blt_1_s, bne_1_s, jump_opcode_selector_1_s;

  beq beq_1 (.ZF(Flags[2]), .S(beq_1_s), .beq(jump_opcode_selector_1_beq));
  b b_1 (.S(b_1_s), .b(jump_opcode_selector_1_b));
  Jump_Opcode_Selector jump_opcode_selector_1 (
    .opcode(opcode), .b(jump_opcode_selector_1_b), .beq(jump_opcode_selector_1_beq),
    .bne(jump_opcode_selector_1_bne), .bge(jump_opcode_selector_1_bge), .ble(jump_opcode_selector_1_ble),
    .bgt(jump_opcode_selector_1_bgt), .blt(jump_opcode_selector_1_blt), .S(jump_opcode_selector_1_s));
  bge bge_1 (.SF(Flags[1]), .OF(Flags[0]), .S(bge_1_s), .bge(jump_opcode_selector_1_bge));
  bne bne_1 (.ZF(Flags[2]), .S(bne_1_s), .bne(jump_opcode_selector_1_bne));
  bgt bgt_1 (.SF(Flags[1]), .OF(Flags[0]), .ZF(Flags[2]), .S(bgt_1_s), .bgt(jump_opcode_selector_1_bgt));
  ble ble_1 (.SF(Flags[1]), .OF(Flags[0]), .ZF(Flags[2]), .S(ble_1_s), .ble(jump_opcode_selector_1_ble));
  blt blt_1 (.SF(Flags[1]), .OF(Flags[0]), .S(blt_1_s), .blt(jump_opcode_selector_1_blt));
  assign nextPCselect = blt_1_s | bgt_1_s | ble_1_s | bge_1_s | bne_1_s | beq_1_s | b_1_s | jump_opcode_selector_1_s;  // OR_Gate or_1, 2 bits wide
endmodule

module Jump_Opcode_Selector (
  input  [3:0] opcode,
  output [1:0] S,
  output b,
  output beq,
  output bne,
  output bge,
  output ble,
  output bgt,
  output blt
);

  wire and_8_out, not_1_out;

  and and_1 (b, opcode[0], ~opcode[1], ~opcode[2], opcode[3]);  // AND_Gate
  and and_2 (beq, ~opcode[0], opcode[1], ~opcode[2], opcode[3]);  // AND_Gate
  and and_3 (bne, opcode[0], opcode[1], ~opcode[2], opcode[3]);  // AND_Gate
  and and_4 (bge, ~opcode[0], ~opcode[1], opcode[2], opcode[3]);  // AND_Gate
  and and_5 (ble, opcode[0], ~opcode[1], opcode[2], opcode[3]);  // AND_Gate
  and and_6 (bgt, ~opcode[0], opcode[1], opcode[2], opcode[3]);  // AND_Gate
  and and_7 (blt, opcode[0], opcode[1], opcode[2], opcode[3]);
  and and_8 (and_8_out, ~b, ~beq, ~bne, ~bge, ~ble, ~bgt, ~blt);  // AND_Gate
  BitSelector #(.width(2), .group(2)) bitselector_1 (.in(2'b11), .out(S), .sel(not_1_out));
  not not_1 (not_1_out, and_8_out);

  // Notes on the sheet:
  //   Sélectionneur d'opération de saut.
endmodule

module b (
  input  b,
  output [1:0] S
);

  wire not_1_out;

  BitSelector #(.width(2), .group(2)) bitselector_1 (.in(2'b10), .out(S), .sel(not_1_out));
  not not_1 (not_1_out, b);

  // Notes on the sheet:
  //   Saut inconditionnel
endmodule

module beq (
  input  ZF,
  input  beq,
  output [1:0] S
);

  wire nand_1_out;

  BitSelector #(.width(2), .group(2)) bitselector_1 (.in(2'b10), .out(S), .sel(nand_1_out));
  nand nand_1 (nand_1_out, ZF, beq);

  // Notes on the sheet:
  //   Opération =
endmodule

module bne (
  input  ZF,
  input  bne,
  output [1:0] S
);

  wire nand_1_out;

  BitSelector #(.width(2), .group(2)) bitselector_1 (.in(2'b10), .out(S), .sel(nand_1_out));
  nand nand_1 (nand_1_out, ~ZF, bne);  // NAND_Gate

  // Notes on the sheet:
  //   Opération !=
endmodule

module bge (
  input  SF,
  input  OF,
  input  bge,
  output [1:0] S
);

  wire nand_1_out, xor_1_out;

  xor xor_1 (xor_1_out, SF, OF);
  BitSelector #(.width(2), .group(2)) bitselector_1 (.in(2'b10), .out(S), .sel(nand_1_out));
  nand nand_1 (nand_1_out, ~xor_1_out, bge);  // NAND_Gate

  // Notes on the sheet:
  //   Opération >=
endmodule

module ble (
  input  SF,
  input  OF,
  input  ZF,
  input  ble,
  output [1:0] S
);

  wire nand_1_out, or_1_out, xor_1_out;

  xor xor_1 (xor_1_out, SF, OF);
  or or_1 (or_1_out, xor_1_out, ZF);
  BitSelector #(.width(2), .group(2)) bitselector_1 (.in(2'b10), .out(S), .sel(nand_1_out));
  nand nand_1 (nand_1_out, or_1_out, ble);

  // Notes on the sheet:
  //   Opération <=
endmodule

module bgt (
  input  SF,
  input  OF,
  input  ZF,
  input  bgt,
  output [1:0] S
);

  wire nand_1_out, or_1_out, xor_1_out;

  xor xor_1 (xor_1_out, SF, OF);
  or or_1 (or_1_out, xor_1_out, ZF);
  BitSelector #(.width(2), .group(2)) bitselector_1 (.in(2'b10), .out(S), .sel(nand_1_out));
  nand nand_1 (nand_1_out, ~or_1_out, bgt);  // NAND_Gate

  // Notes on the sheet:
  //   Opération >
endmodule

module blt (
  input  SF,
  input  OF,
  input  blt,
  output [1:0] S
);

  wire nand_1_out, xor_1_out;

  xor xor_1 (xor_1_out, SF, OF);
  nand nand_1 (nand_1_out, xor_1_out, blt);
  BitSelector #(.width(2), .group(2)) bitselector_1 (.in(2'b10), .out(S), .sel(nand_1_out));

  // Notes on the sheet:
  //   Opération <
endmodule
