// Logisim project SC1.circ as structural Verilog: 1 circuit, main circuit main
module main (
  input  RESET
);

  wire clock_1_out, main_2_isjmp, main_2_isload, main_2_regwrite;
  wire [1:0] main_7_nextpcselect;
  wire [2:0] main_2_ctrual;
  wire [3:0] main_3_rd, main_3_rs, main_3_rt, main_6_cf__zf__sf__of, ram_1_data_2;
  wire [7:0] adder_1_out, adder_2_out, main_1_out_4, main_4_r___rs, main_4_r___rt, main_5_out_2, main_6_s,
       multiplexer_1_out, multiplexer_2_out;
  wire [11:0] ram_1_data;

  compteur_de_bits_main main_1 (.in_1(multiplexer_2_out), .RESET(RESET), .out_4(main_1_out_4), .CLOCK(clock_1_out));
  Clock clock_1 (.out(clock_1_out));
  Adder adder_1 (.a(main_1_out_4), .b(8'h1), .out(adder_1_out));  // open: cin, cout
  RAM #(.dataWidth(16)) ram_1 (
    .addr(main_1_out_4), .data({ram_1_data_2, ram_1_data}), .clk(clock_1_out));  // open: sel, ld, clr
  Decodeur_d_instruction_main main_2 (
    .OPcode(ram_1_data_2), .isJMP(main_2_isjmp), .regWrite(main_2_regwrite), .isLoad(main_2_isload),
    .ctrUAL(main_2_ctrual));
  Selection_registres_main main_3 (
    .isJMP(main_2_isjmp), ._11_8(ram_1_data[11:8]), ._7_4(ram_1_data[7:4]), ._3_0(ram_1_data[3:0]),
    .rd(main_3_rd), .rs(main_3_rs), .rt(main_3_rt));
  Multiplexer #(.width(8)) multiplexer_1 (
    .in0(main_6_s), .in1(ram_1_data[7:0]), .out(multiplexer_1_out), .sel(main_2_isload));  // open: en
  Banc_de_registre_main main_4 (
    .rd(main_3_rd), .rt(main_3_rs), .rs(main_3_rt), .ValIn(multiplexer_1_out), .R___rt(main_4_r___rt),
    .R___rs(main_4_r___rs), .Reset(RESET), .Horloge(clock_1_out), .regWrite(main_2_regwrite));
  SigneExt_main main_5 (.out_2(main_5_out_2), .offset(ram_1_data[3:0]));
  Adder adder_2 (.a(adder_1_out), .b(main_5_out_2), .out(adder_2_out));  // open: cin, cout
  UAL_main main_6 (
    .Rs(main_4_r___rt), .Rt(main_4_r___rs), .ctrUAL(main_2_ctrual), .S(main_6_s),
    .CF__ZF__SF__OF(main_6_cf__zf__sf__of));
  Multiplexer #(.select(2), .width(8)) multiplexer_2 (
    .in0(adder_1_out), .in1({8{1'b1}}), .in2(adder_2_out), .out(multiplexer_2_out), .sel(main_7_nextpcselect));  // open: in3, en
  Jump_Controler_main main_7 (.flags(main_6_cf__zf__sf__of), .opcode(ram_1_data_2), .nextPCselect(main_7_nextpcselect));

  // Notes on the sheet:
  //   { Horloge }
  //   0xFF
  //   "instruction suivante"
  //   "HALT"
  //   <15:12>
  //   {op}
  //   isJMP
  //   regWrite
  //   valIn
  //   <11:8>
  //   <7:4>
  //   {rd/rs}
  //   {rs/rt}
  //   rd
  //   rs
  //   isLoad
  //   <3:0>
  //   {rt}
  //   rt
  //   <7:0>
  //   {val}
  //   Rs
  //   Rt
  //   "saut"
  //   ctrUAL
  //   CF, ZF, SF, OF
  //   nextPCselect
endmodule
