// Logisim project Selection_registres.circ as structural Verilog: 1 circuit, main circuit main
module main (
  input  [3:0] _11_8,
  input  [3:0] _7_4,
  input  [3:0] _3_0,
  input  isJMP,
  output [3:0] rd,
  output [3:0] rs,
  output [3:0] rt
);

  Multiplexer #(.width(4)) multiplexer_1 (.in0(_11_8), .in1(4'b0000), .out(rd), .sel(isJMP));  // open: en
  Multiplexer #(.width(4)) multiplexer_2 (.in0(_7_4), .in1(_11_8), .out(rs), .sel(isJMP));  // open: en
  Multiplexer #(.width(4)) multiplexer_3 (.in0(_3_0), .in1(_7_4), .out(rt), .sel(isJMP));  // open: en
endmodule
