// Logisim project SigneExt.circ as structural Verilog: 1 circuit, main circuit main
module main (
  input  [3:0] offset,
  output [7:0] out_2
);

  assign out_2 = {{4{offset[3]}}, offset};  // Bit_Extender bit_extender_1
endmodule
