// Logisim project UAL.circ as structural Verilog: 14 circuits, main circuit main
module main (
  input  [7:0] Rs,
  input  [7:0] Rt,
  input  [2:0] ctrUAL,
  output [7:0] S,
  output [3:0] CF__ZF__SF__OF
);

  wire bitselector_1_out, bitselector_2_out, bitselector_10_out, bitselector_11_out,
       decoderctrual_1_decaldroite, decoderctrual_1_decalgauche, decoderctrual_1_et8bits,
       decoderctrual_1_non8bits, decoderctrual_1_ou8bits, overflow_1_of_plus, overflow_2_of_minus, Radd,
       Rsous, Sadd, Ssous;
  wire [7:0] add, \add8bits_1_résultat_add , and8bits_1_sortie_and, DecalD8, DecalG8, et8, non8,
       \not8bits_1_négation , or8bits_1_sortie_ou, ou8, shiftl8bits_1_out_2, shiftr8bits_1_out_2, sou,
       \sub8bits_1_résultat_sous ;

  Add8bits add8bits_1 (.A(Rs), .B(Rt), .\Résultat_ADD (\add8bits_1_résultat_add ), .R(Radd));
  Sub8bits sub8bits_1 (.A(Rs), .B(Rt), .\Résultat_SOUS (\sub8bits_1_résultat_sous ), .R(Rsous));
  Or8bits or8bits_1 (.A(Rs), .B(Rs), .Sortie_OU(or8bits_1_sortie_ou));
  And8bits and8bits_1 (.A(Rt), .B(Rs), .Sortie_AND(and8bits_1_sortie_and));
  Not8bits not8bits_1 (.A(Rs), .\Négation (\not8bits_1_négation ));
  ShiftL8bits shiftl8bits_1 (.in_1(Rs), .out_2(shiftl8bits_1_out_2));
  ShiftR8bits shiftr8bits_1 (.in_1(Rs), .out_2(shiftr8bits_1_out_2));
  DecoderCtrUAL decoderctrual_1 (
    .add(Sadd), .sous(Ssous), .ou8bits(decoderctrual_1_ou8bits), .et8bits(decoderctrual_1_et8bits),
    .non8bits(decoderctrual_1_non8bits), .decalGauche(decoderctrual_1_decalgauche),
    .DecalDroite(decoderctrual_1_decaldroite), .OPcode(ctrUAL));
  Overflow overflow_1 (.A(Rs[7]), .B(Rt[7]), .SF(CF__ZF__SF__OF[1]), .OF_plus(overflow_1_of_plus));
  BitSelector #(.width(1)) bitselector_1 (.in(overflow_1_of_plus), .out(bitselector_1_out), .sel(Sadd));
  BitSelector #(.width(1)) bitselector_2 (.in(overflow_2_of_minus), .out(bitselector_2_out), .sel(Ssous));
  Overflow_2 overflow_2 (.A(Rs[7]), .B(Rt[7]), .SF(CF__ZF__SF__OF[1]), .OF_minus(overflow_2_of_minus));
  BitSelector #(.group(8)) bitselector_3 (.in(\add8bits_1_résultat_add ), .out(add), .sel(Sadd));
  BitSelector #(.group(8)) bitselector_4 (.in(\sub8bits_1_résultat_sous ), .out(sou), .sel(Ssous));
  BitSelector #(.group(8)) bitselector_5 (.in(or8bits_1_sortie_ou), .out(ou8), .sel(decoderctrual_1_ou8bits));
  BitSelector #(.group(8)) bitselector_6 (.in(and8bits_1_sortie_and), .out(et8), .sel(decoderctrual_1_et8bits));
  BitSelector #(.group(8)) bitselector_7 (.in(\not8bits_1_négation ), .out(non8), .sel(decoderctrual_1_non8bits));
  BitSelector #(.group(8)) bitselector_8 (.in(shiftl8bits_1_out_2), .out(DecalG8), .sel(decoderctrual_1_decalgauche));
  BitSelector #(.group(8)) bitselector_9 (.in(shiftr8bits_1_out_2), .out(DecalD8), .sel(decoderctrual_1_decaldroite));
  or or_1 (CF__ZF__SF__OF[0], bitselector_1_out, bitselector_2_out);
  Zero8bits zero8bits_1 (.A({CF__ZF__SF__OF[1], S[6:0]}), .S(CF__ZF__SF__OF[2]));
  BitSelector #(.width(1)) bitselector_10 (.in(Radd), .out(bitselector_10_out), .sel(Sadd));
  BitSelector #(.width(1)) bitselector_11 (.in(Rsous), .out(bitselector_11_out), .sel(Ssous));
  or or_2 (CF__ZF__SF__OF[3], bitselector_10_out, bitselector_11_out);
  assign {CF__ZF__SF__OF[1], S[6:0]} = add | sou | ou8 | et8 | non8 | DecalG8 | DecalD8;  // OR_Gate or_3, 8 bits wide

  assign S[7] = CF__ZF__SF__OF[1];

  // Other names for the same wires on the sheet: OF = CF__ZF__SF__OF[0]; ZF = CF__ZF__SF__OF[2];
  //   CF = CF__ZF__SF__OF[3]; bitPoidsFortA = Rs[7]; bitPoidsFortB = Rt[7]; S8bits[7:0] = {CF__ZF__SF__OF[1], S[6:0]};
  //   SF = CF__ZF__SF__OF[1]

  // Notes on the sheet:
  //   Opération Arithmétique
  //   Circuit de l'overflow
  //   Circuit du zero flow
  //   Circuit des flags de sortie
  //   Circuit du carryflow
  //   Circuit de séléction du résultat du calcule
endmodule

module Or8bits (
  input  [7:0] A,
  input  [7:0] B,
  output [7:0] Sortie_OU
);

  or or_1 (Sortie_OU[0], A[0], B[0]);
  or or_2 (Sortie_OU[1], A[1], B[1]);
  or or_3 (Sortie_OU[2], A[2], B[2]);
  or or_4 (Sortie_OU[3], A[3], B[3]);
  or or_5 (Sortie_OU[4], A[4], B[4]);
  or or_6 (Sortie_OU[5], A[5], B[5]);
  or or_7 (Sortie_OU[6], A[6], B[6]);
  or or_8 (Sortie_OU[7], A[7], B[7]);
endmodule

module Add8bits (
  input  [7:0] A,
  input  [7:0] B,
  output [7:0] \Résultat_ADD ,
  output R
);

  wire adder_1_cout, adder_2_cout, adder_3_cout, adder_4_cout, adder_5_cout, adder_6_cout, adder_7_cout;

  Adder #(.width(1)) adder_1 (.a(A[0]), .b(B[0]), .out(\Résultat_ADD [0]), .cin(1'b0), .cout(adder_1_cout));
  Adder #(.width(1)) adder_2 (.a(A[1]), .b(B[1]), .out(\Résultat_ADD [1]), .cin(adder_1_cout), .cout(adder_2_cout));
  Adder #(.width(1)) adder_3 (.a(A[2]), .b(B[2]), .out(\Résultat_ADD [2]), .cin(adder_2_cout), .cout(adder_3_cout));
  Adder #(.width(1)) adder_4 (.a(A[3]), .b(B[3]), .out(\Résultat_ADD [3]), .cin(adder_3_cout), .cout(adder_4_cout));
  Adder #(.width(1)) adder_5 (.a(A[4]), .b(B[4]), .out(\Résultat_ADD [4]), .cin(adder_4_cout), .cout(adder_5_cout));
  Adder #(.width(1)) adder_6 (.a(A[5]), .b(B[5]), .out(\Résultat_ADD [5]), .cin(adder_5_cout), .cout(adder_6_cout));
  Adder #(.width(1)) adder_7 (.a(A[6]), .b(B[6]), .out(\Résultat_ADD [6]), .cin(adder_6_cout), .cout(adder_7_cout));
  Adder #(.width(1)) adder_8 (.a(A[7]), .b(B[7]), .out(\Résultat_ADD [7]), .cin(adder_7_cout), .cout(R));
endmodule

module And8bits (
  input  [7:0] A,
  input  [7:0] B,
  output [7:0] Sortie_AND
);

  and and_1 (Sortie_AND[0], A[0], B[0]);
  and and_2 (Sortie_AND[1], A[1], B[1]);
  and and_3 (Sortie_AND[2], A[2], B[2]);
  and and_4 (Sortie_AND[3], A[3], B[3]);
  and and_5 (Sortie_AND[4], A[4], B[4]);
  and and_6 (Sortie_AND[5], A[5], B[5]);
  and and_7 (Sortie_AND[6], A[6], B[6]);
  and and_8 (Sortie_AND[7], A[7], B[7]);
endmodule

module Not8bits (
  input  [7:0] A,
  output [7:0] \Négation 
);

  not not_1 (\Négation [0], A[0]);
  not not_2 (\Négation [1], A[1]);
  not not_3 (\Négation [2], A[2]);
  not not_4 (\Négation [3], A[3]);
  not not_5 (\Négation [4], A[4]);
  not not_6 (\Négation [5], A[5]);
  not not_7 (\Négation [6], A[6]);
  not not_8 (\Négation [7], A[7]);
endmodule

module Comp2 (
  input  [7:0] A,
  output [7:0] \Comp_à_2 
);

  wire [7:0] \not8bits_1_négation ;
  wire [7:7] \add8bits_1_résultat_add ;

  Not8bits not8bits_1 (.A(A), .\Négation (\not8bits_1_négation ));
  Add8bits add8bits_1 (
    .A(\not8bits_1_négation ), .B(8'h1), .\Résultat_ADD ({\add8bits_1_résultat_add [7], \Comp_à_2 [6:0]}));  // open: R

  assign \Comp_à_2 [7] = A[7];

  // Notes on the sheet:
  //   Comme on travaille en bit à magnitude signé, on récupère le bit de poids fort pour directement l'insérer dans le résultat.
  //   On garde ainsi la valeur du bit de poids fort intacte dans le complément.
endmodule

module Zero8bits (
  input  [7:0] A,
  output S
);

  wire or_1_out;

  or or_1 (or_1_out, A[0], A[1], A[2], A[3], A[4], A[5], A[6], A[7]);
  not not_1 (S, or_1_out);
endmodule

module Overflow (
  input  A,
  input  B,
  input  SF,
  output OF_plus
);

  wire and_1_out, and_2_out;

  and and_1 (and_1_out, A, B, ~SF);  // AND_Gate
  and and_2 (and_2_out, ~A, ~B, SF);  // AND_Gate
  or or_1 (OF_plus, and_1_out, and_2_out);
endmodule

module Overflow_2 (
  input  A,
  input  B,
  input  SF,
  output OF_minus
);

  wire and_1_out, and_2_out;

  and and_1 (and_1_out, A, ~B, ~SF);  // AND_Gate
  and and_2 (and_2_out, ~A, B, SF);  // AND_Gate
  or or_1 (OF_minus, and_1_out, and_2_out);
endmodule

module Sub8bits (
  input  [7:0] A,
  input  [7:0] B,
  output [7:0] \Résultat_SOUS ,
  output R
);

  Subtractor subtractor_1 (.a(A), .b(B), .out(\Résultat_SOUS ), .bin(1'b0), .bout(R));
endmodule

module ShiftR8bits (
  input  [7:0] in_1,
  output [7:0] out_2
);

  Shifter #(.shift("lr")) shifter_1 (.in(in_1), .\dist (3'b001), .out(out_2));
endmodule

module ShiftL8bits (
  input  [7:0] in_1,
  output [7:0] out_2
);

  Shifter shifter_1 (.in(in_1), .\dist (3'b001), .out(out_2));

  // Notes on the sheet:
  //   Le bit de poids fort est redirigé vers la sortie du bit de bit faible.
endmodule

module DecoderCtrUAL (
  input  [2:0] OPcode,
  output add,
  output sous,
  output ou8bits,
  output et8bits,
  output non8bits,
  output decalGauche,
  output DecalDroite
);

  wire and_1_out, and_2_out, and_3_out, and_4_out, and_5_out, and_6_out, and_7_out;

  not not_1 (add, and_1_out);
  and and_1 (and_1_out, ~OPcode[0], ~OPcode[1], ~OPcode[2]);  // AND_Gate
  not not_2 (sous, and_2_out);
  and and_2 (and_2_out, OPcode[0], ~OPcode[1], ~OPcode[2]);  // AND_Gate
  not not_3 (ou8bits, and_3_out);
  and and_3 (and_3_out, ~OPcode[0], OPcode[1], ~OPcode[2]);  // AND_Gate
  not not_4 (et8bits, and_4_out);
  and and_4 (and_4_out, OPcode[0], OPcode[1], ~OPcode[2]);  // AND_Gate
  not not_5 (non8bits, and_5_out);
  and and_5 (and_5_out, ~OPcode[0], ~OPcode[1], OPcode[2]);  // AND_Gate
  not not_6 (decalGauche, and_6_out);
  and and_6 (and_6_out, OPcode[0], ~OPcode[1], OPcode[2]);  // AND_Gate
  not not_7 (DecalDroite, and_7_out);
  and and_7 (and_7_out, ~OPcode[0], OPcode[1], OPcode[2]);  // AND_Gate
endmodule

module test (
  input  [7:0] in_1,
  input  [7:0] in_2,
  input  [7:0] in_3,
  input  [2:0] in_4,
  input  [7:0] in_5,
  input  [2:0] in_6,
  output [7:0] out_7,
  output [7:0] out_8,
  output [7:0] out_9,
  output [7:0] out_10
);

  ShiftR8bits shiftr8bits_1 (.in_1(in_1), .out_2(out_7));
  ShiftL8bits shiftl8bits_1 (.in_1(in_2), .out_2(out_8));
  Shifter shifter_1 (.in(in_3), .\dist (in_4), .out(out_9));
  Shifter #(.shift("lr")) shifter_2 (.in(in_5), .\dist (in_6), .out(out_10));
endmodule
