// Logisim project compteur de bits.circ as structural Verilog: 1 circuit, main circuit main
module main (
  input  [7:0] in_1,
  input  RESET,
  input  CLOCK,
  output [7:0] out_4
);

  Register register_1 (.D(in_1), .Q(out_4), .clk(CLOCK), .clr(RESET));  // open: en
endmodule
